# Fritzing sketch Sketch (saved by Fritzing 0.9.3b)
circuit board: 8.46667cm x 5.64444cm
breadboards: 1

parts:
  part = WeMos D1 Mini [part_number=1]
  LED1 = ws2812b [package="smd 2812b"]
  F = RFID-RC522-v2

nets:
  3V3: part.3V3, LED1.VDD, F.3.3V
  N1: part.D1, F.RST
  N2: part.D2, LED1.DIN
  N3: part.D4, F.SDA
  N4: part.D5, F.SCK
  N5: part.D6, F.MISO
  N6: part.D7, F.MOSI
  VSS: part.G, LED1.VSS, F.GND

custom parts:
  RFID-RC522-v2: A simple China made RFID-RC522 Reader; do check the pin labels, as this is a MFRC522 based clone.
